# Fritzing sketch sheet with LDC (saved by Fritzing 0.8.3b)
breadboards: 1

parts:
  LCD1 = LCD screen
  Shield = Arduino Ethernet Shield (Rev3)
  R1 = Photocell (LDR) [package=THT]
  R2 = Resistor [tolerance=±5% resistance=1k package=THT]
  T1 = LM35 Temperature Sensor [package="TO92 [THT]"]
  R3 = Rotary Potentiometer (Small)
  R4 = Resistor [tolerance=±5% resistance=220 package=THT]

nets:
  GND: LCD1.VSS, LCD1.LED-, Shield.GND, R2.Pin_0, T1.GND, R3.leg2, R4.Pin_0
  VDD: LCD1.VDD, Shield.5V, R1.pin_1, T1.+Vs, R3.leg1
  N1: LCD1.V0, R3.wiper
  N2: LCD1.RS, Shield.PWM_D9
  N3: LCD1.R/W, Shield.D8
  N4: LCD1.DB4, Shield.PWM_D5
  N5: LCD1.DB5, Shield.SDCS
  N6: LCD1.DB6, Shield.PWM_D3
  N7: LCD1.DB7, Shield.D2
  N8: LCD1.LED+, R4.Pin_1
  N9: Shield.A0, T1.Vout
  N10: Shield.A1, R1.pin_0, R2.Pin_1
