# Fritzing sketch sheet (saved by Fritzing 0.8.3b)
breadboards: 1

parts:
  Shield = Arduino Ethernet Shield (Rev3)
  R1 = Photocell (LDR) [package=THT]
  R2 = Resistor [tolerance=±5% resistance=1k package=THT]
  T1 = LM35 Temperature Sensor [package="TO92 [THT]"]

nets:
  N1: Shield.A0, T1.Vout
  N2: Shield.A1, R1.pin_0, R2.Pin_1
  N3: Shield.5V, R1.pin_1, T1.+Vs
  GND: Shield.GND, R2.Pin_0, T1.GND
